# Fritzing sketch schema (saved by Fritzing 0.9.3b)

parts:
  PR1 = PHOTOCELL [package=photocell]
  PR2 = PHOTOCELL [package=photocell]
  PR3 = PHOTOCELL [package=photocell]
  PR4 = PHOTOCELL [package=photocell]
  PR5 = PHOTOCELL [package=photocell]
  PR6 = PHOTOCELL [package=photocell]
  PR7 = PHOTOCELL [package=photocell]
  PR9 = PHOTOCELL [package=photocell]
  PR8 = PHOTOCELL [package=photocell]
  R1 = Resistor [tolerance=±5% resistance=10k package=THT]
  R2 = Resistor [tolerance=±5% resistance=10k package=THT]
  R3 = Resistor [tolerance=±5% resistance=10k package=THT]
  D1 = Diode [package=diode-1n4148]
  D2 = Diode [package=diode-1n4148]
  D3 = Diode [package=diode-1n4148]
  D4 = Diode [package=diode-1n4148]
  D5 = Diode [package=diode-1n4148]
  D6 = Diode [package=diode-1n4148]
  D7 = Diode [package=diode-1n4148]
  D8 = Diode [package=diode-1n4148]
  D9 = Diode [package=diode-1n4148]
  Arduino = Arduino Uno (Rev3) - ICSP

nets:
  N1: PR1.P$1, PR2.P$1, PR3.P$1, Arduino.D4
  N2: PR1.P$2, D1.A
  N3: PR2.P$2, D2.A
  N4: PR3.P$2, D3.A
  N5: PR4.P$1, PR5.P$1, PR6.P$1, Arduino.D3_PWM
  N6: PR4.P$2, D4.A
  N7: PR5.P$2, D5.A
  N8: PR6.P$2, D6.A
  N9: PR7.P$1, PR9.P$1, PR8.P$1, Arduino.D2
  N10: PR7.P$2, D7.A
  N11: PR9.P$2, D9.A
  N12: PR8.P$2, D8.A
  N13: R1.Pin_0, D1.C, D4.C, D7.C, Arduino.A0
  N14: R1.Pin_1, R2.Pin_1, R3.Pin_1, Arduino.GND
  N15: R2.Pin_0, D2.C, D5.C, D8.C, Arduino.A1
  N16: R3.Pin_0, D3.C, D6.C, D9.C, Arduino.A2
